// Digital circuit RV5-PROCESSOR.dig as structural Verilog
module RV5_PROCESSOR (
  input  clock
);

  wire a_eq_b, a_lt_b, branch_sel, carry, csr_opclear, csr_opset, csr_useimm, csr_wen, d_memwen, d_memwen_t,
       d_regwen, d_regwen_t, dm_mem_wen, dret_sel, ebreak_sel, ecall_sel, haltreq, IF_jal_sel, IF_jalr_sel,
       IF_mret_sel, is_debug, is_progbuf, jump_progbuf, resumereq;
  wire [1:0] rv5_control_logic_1_alu_asel, rv5_control_logic_1_wb_sel;
  wire [2:0] funct3, rv5_control_logic_1_alu_op, rv5_control_logic_1_imm_sel;
  wire [4:0] d_rd, d_rd_t, d_rs1, d_rs1_t;
  wire [6:0] inst;
  wire [6:3] rv5_control_logic_1_ld_signext;
  wire [6:5] rv5_control_logic_1_alu_mod;
  wire [11:0] funct12;
  wire [31:0] alu_out, and_1_out, csr_out, d_rdin, d_rdin_t, dcsr, dm_mem_addr, dm_mem_rdata, dm_mem_wdata,
       dpc, ID_pc, IF_imm_signext, IF_mepc, IF_mtvec, multiplexer_1_out, multiplexer_2_out,
       multiplexer_3_out, multiplexer_4_out, multiplexer_5_out, not_1_out, or_1_out, ra, rv5_gpr_1_p8,
       rv5_memory_1_p13;
  wire [31:2] add_1_s;

  RV5_DEBUG_MODULE rv5_debug_module_1 (
    .clk(clock), .dcsr(dcsr), .dm_mem_rdata(dm_mem_rdata), .ra(ra), .is_debug(is_debug),
    .is_progbuf(is_progbuf), .d_regwen(d_regwen), .d_rdin(d_rdin), .d_memwen(d_memwen), .d_rd(d_rd),
    .d_rs1(d_rs1), .haltreq(haltreq), .resumereq(resumereq), .jump_progbuf(jump_progbuf),
    .dm_mem_wdata(dm_mem_wdata), .dm_mem_wen(dm_mem_wen), .dm_mem_addr(dm_mem_addr), .d_regwen_2(d_regwen_t),
    .d_rdin_2(d_rdin_t), .d_memwen_2(d_memwen_t), .d_rd_2(d_rd_t), .d_rs1_2(d_rs1_t));
  // RV5_PCU rv5_pcu_1: pin names not known; wires that end beside it: IF_imm_signext, alu_out, IF_mtvec, IF_mepc, dpc, branch_sel, IF_jal_sel, IF_jalr_sel, ecall_sel, IF_mret_sel, dcsr, dret_sel, haltreq, jump_progbuf, resumereq, ebreak_sel, funct3, a_eq_b, a_lt_b, carry, clock, ID_pc, is_debug, is_progbuf
  Multiplexer #(.Bits(32)) multiplexer_1 (
    .sel(csr_useimm), .in_0(ra), .in_1({{27{1'b0}}, d_rs1}), .out(multiplexer_1_out));
  assign and_1_out = not_1_out & csr_out;  // And and_1, 32 bits wide
  assign not_1_out = ~multiplexer_1_out;  // Not not_1, 32 bits wide
  assign or_1_out = multiplexer_1_out | csr_out;  // Or or_1, 32 bits wide
  RV5_CONTROL_LOGIC rv5_control_logic_1 (
    .opcode(inst), .funct3(funct3), .funct12(funct12), .imm_sel(rv5_control_logic_1_imm_sel),
    .reg_wen(d_regwen), .wb_sel(rv5_control_logic_1_wb_sel), .ram_wen(d_memwen),
    .ram_ren(rv5_control_logic_1_ld_signext[3]), .ram_b(rv5_control_logic_1_ld_signext[4]),
    .ram_h(rv5_control_logic_1_ld_signext[5]), .ld_signext(rv5_control_logic_1_ld_signext[6]),
    .alu_asel(rv5_control_logic_1_alu_asel), .alu_op(rv5_control_logic_1_alu_op),
    .alu_bsel(rv5_control_logic_1_alu_mod[5]), .alu_mod(rv5_control_logic_1_alu_mod[6]),
    .branch_sel(branch_sel), .jal_sel(IF_jal_sel), .jalr_sel(IF_jalr_sel), .csr_wen(csr_wen),
    .csr_opset(csr_opset), .csr_opclear(csr_opclear), .csr_useimm(csr_useimm), .ecall_sel(ecall_sel),
    .ebreak_sel(ebreak_sel), .mret_sel(IF_mret_sel), .dret_sel(dret_sel));
  Multiplexer #(.Bits(32)) multiplexer_2 (
    .sel(csr_opclear), .in_0(multiplexer_1_out), .in_1(and_1_out), .out(multiplexer_2_out));
  Multiplexer #(.Bits(32)) multiplexer_3 (
    .sel(csr_opset), .in_0(multiplexer_2_out), .in_1(or_1_out), .out(multiplexer_3_out));
  RV5_IMM_GEN rv5_imm_gen_1 (
    .INSTR_32({funct12, d_rs1, funct3, d_rd, inst}), .imm_sel(rv5_control_logic_1_imm_sel),
    .imm(IF_imm_signext));
  // RV5_CSR rv5_csr_1: pin names not known; wires that end beside it: clock, funct12, multiplexer_3_out, csr_wen, ID_pc, ecall_sel, IF_mret_sel, ebreak_sel, is_debug, haltreq, csr_out, IF_mepc, IF_mtvec, dcsr, dpc
  // RV5_GPR rv5_gpr_1: pin names not known; wires that end beside it: d_rs1_t, funct12[4:0], d_rdin_t, clock, d_rd_t, d_regwen_t, ra, rv5_gpr_1_p8
  Multiplexer #(.Bits(32)) multiplexer_4 (
    .sel(rv5_control_logic_1_alu_mod[5]), .in_0(rv5_gpr_1_p8), .in_1(IF_imm_signext), .out(multiplexer_4_out));
  Multiplexer #(.Selector_Bits(2), .Bits(32)) multiplexer_5 (
    .sel(rv5_control_logic_1_alu_asel), .in_0(ra), .in_1(ID_pc), .in_2({32{1'b0}}), .in_3({32{1'b0}}),
    .out(multiplexer_5_out));
  RV5_ALU rv5_alu_1 (
    .OP(rv5_control_logic_1_alu_op), .AoB(alu_out), .A(multiplexer_5_out), .B(multiplexer_4_out),
    .MOD(rv5_control_logic_1_alu_mod[6]), .A_eq_B(a_eq_b), .A_lt_B(a_lt_b), .CRY(carry));
  // RV5_MEMORY rv5_memory_1: pin names not known; wires that end beside it: alu_out, rv5_gpr_1_p8, d_memwen_t, rv5_control_logic_1_ld_signext[3], clock, rv5_control_logic_1_ld_signext[4], rv5_control_logic_1_ld_signext[5], rv5_control_logic_1_ld_signext[6], ID_pc, dm_mem_addr, dm_mem_wen, dm_mem_wdata, rv5_memory_1_p13, {funct12, d_rs1, funct3, d_rd, inst}, dm_mem_rdata
  Add #(.Bits(30)) add_1 (.a(ID_pc[31:2]), .b({30{1'b0}}), .c_i(1'b1), .s(add_1_s));  // open: c_o
  Multiplexer #(.Selector_Bits(2), .Bits(32)) multiplexer_6 (
    .sel(rv5_control_logic_1_wb_sel), .in_0(alu_out), .in_1({add_1_s, 2'b00}), .in_2(rv5_memory_1_p13),
    .in_3(csr_out), .out(d_rdin));

  // Other names for the same wires on the sheet: IF_a_eq_b = a_eq_b; IF_a_lt_b = a_lt_b; IF_alu_out[31:0] = alu_out;
  //   IF_branch_sel = branch_sel; IF_carry = carry; clk = clock; IF_dcsr[31:0] = dcsr; IF_dpc[31:0] = dpc;
  //   IF_dret_sel = dret_sel; IF_ebreak_sel = ebreak_sel; IF_ecall_sel = ecall_sel;
  //   imm_signext[31:0] = IF_imm_signext; inst[31:7] = {funct12, d_rs1, funct3, d_rd}; IF_funct3[2:0] = funct3;
  //   rs1[4:0] = d_rs1; jal_sel = IF_jal_sel; jalr_sel = IF_jalr_sel; mepc[31:0] = IF_mtvec; mret_sel = IF_mret_sel;
  //   mtvec[31:0] = IF_mepc; pc[31:0] = ID_pc; ID_wb[31:0] = d_rdin; wb[31:0] = d_rdin

  // Notes on the sheet:
  //   clock: Hz: 5000
  //   Note: In the debug module I have
  //   something set-up to override
  //   this clock to maximum when debug
  //   work needs to be done.
  //   It's definitely a hack but worth it
  //   for the debugging performance.
  //   TLDR: The clock speed that you set 
  //   here really just dictates how 
  //   fast it will go *most* of the time.
  //   RISC-V CPU:
  //   IF: Instruction fetch
  //   In a Harvard-style CPU, there would
  //   be actual instruction memory here.
  //   Instead, we have a tunnel to our
  //   memory block and a tunnel back.
  //   This is a good compromise for us.
  //   However, another option is doing
  //   a fetch/execute design, where
  //   we spend a clock cycle getting the
  //   instruction and then another using it.
  //   (Or, of course, we could pipeline
  //   this processor.)
  //   About the CPU
  //   This is a single-cycle RV32I processor. In addition to the base instruction set, it also implements
  //   the Ziscr extension and contains a debug module.
  //   Although it is single-cycle, it is organized according to pipeline stages. 
  //   Tunnels that cross stages are aliased as prefixed with their destination stage; for example, alu-out
  //   becomes IF-alu-out when crossing into the IF stage. Because this CPU is single-cycle, these tunnels
  //   are equivilent, and at this point it is simply an organizational tool.
  //   Additionally, this is a Von Neumann architecture, and so instruction memory and data memory are
  //   merged. This makes it look slightly different than some educational datapath diagrams you might
  //   see, which sometimes show the Harvard style.
  //   ID: Instruction decode/register file read
  //   Involved with the Ziscr extension.
  //   debug module stuff - ignore
  //   (unless curious)
  //   RALU
  //   EX: Execute/address calculation
  //   MEM: Memory access
  //   WB: Write back
endmodule
